# Fritzing sketch meteo (saved by Fritzing 0.9.2b)
circuit board: 12.9897cm x 1.91301cm

parts:
  Part2 = Arduino Pro Mini Atmega328
  Pad1 = Pad [width=8.15921693659805 height=1.78833629826251 connect=center]
  Pad2 = Pad [width=8.15921693659805 height=1.78833629826251 connect=center]  # not connected
  Pad3 = Pad [width=8.15921693659805 height=1.78833629826251 connect=center]
  Pad4 = Pad [width=8.15921693659805 height=1.78833629826251 connect=center]
  S1 = Tilt Switch [package=THT]
  U1 = A23 battery [package=battery-a23]
  7_Segment_4_Digit_Display1 = 7-segment-4-digit-common-cathode-display [part_number=CA56-12SRWA package=7-segment-4digit-cathode]  # not connected

nets:
  N1: Part2.A6, S1.Pin_1
  N2: Part2.A7, Pad3.pad
  N3: Part2.GND#24, U1.-1, U1.-2
  N4: Part2.RAW, U1.+1, U1.+2
  N5: Part2.VCC, Pad1.pad
  N6: Part2.GND#45, Pad4.pad, S1.Pin_2

custom parts:
  Arduino Pro Mini Atmega328: Arduino Pro Mini based on Atmega328. This is a 5V Arduino running the 16MHz bootloader. There is a voltage regulator on board so it can accept voltage up to 12VDC. If you're supplying unregulated power to the board, be sure to connect to the "RAW" pin on not VCC.
  A23 battery: A23 battery (Duracell MN21 and Keystone holders No82)
  7-segment-4-digit-common-cathode-display: A 7 Segment 4 Digit common cathode display, with decimal points
